# Fritzing sketch ArduinoUno_Slider_LED (saved by Fritzing 0.9.2b)

parts:
  Part1 = Arduino Uno (Rev3)
  LED1 = LED - 5mm [color="Red (633nm)" package="5 mm [THT]"]
  R1 = Slide Potentiometer [maximum_resistance=100kΩ]

nets:
  N1: Part1.A0, R1.wiper
  N2: Part1.D13/SCK, LED1.anode
  N3: Part1.GND, LED1.cathode, R1.leg2
  N4: Part1.5V, R1.leg1
