# Fritzing sketch schematic-arduino-uno-nordic-nrf24l01 (saved by Fritzing 0.9.2b)

parts:
  Part1 = Arduino Uno (Rev3) - ICSP
  NRF24L1 = NRF24L01
  LED1 = LEDs [package=led10mm]

nets:
  N1: Part1.D9_PWM, NRF24L1.CE
  N2: Part1.D10_PWM/SS, NRF24L1.CSN
  N3: Part1.D11_PWM/MOSI, NRF24L1.MOSI
  N4: Part1.D12/MISO, NRF24L1.MISO
  N5: Part1.D13/SCK, NRF24L1.SCK
  N6: Part1.D3_PWM, LED1.C
  3V3: Part1.3V3, NRF24L1.VCC
  GND: Part1.GND, NRF24L1.GND, LED1.A

custom parts:
  NRF24L01: NRF24L01 module
